# Fritzing sketch sketch (saved by Fritzing 0.9.3b)
breadboards: 2

parts:
  U2 = ESP8266 NodeMCU LoLin module
  DHT1 = Humidity and Temperature Sensor DHT11
  S1 = Tilt Switch [package=THT]
  LED1 = LED - 5mm [color="Red (633nm)" package="5 mm [THT]"]
  LED2 = LED - 5mm [color="Yellow (595nm)" package="5 mm [THT]"]
  R2 = Resistor [tolerance=±5% resistance=200 package=THT]
  R3 = Resistor [tolerance=±5% resistance=200 package=THT]
  Componente1 = LCD1602-I2C
  R1 = Resistor [tolerance=±5% resistance=10k package="0603 [SMD]"]
  U3 = ESP8266 NodeMCU LoLin module
  S2 = Tilt Switch [package=THT]

nets:
  N1: U2.D1, Componente1.SCL
  N2: U2.D2, Componente1.SDA
  N3: U2.D3, DHT1.Data-signal, R1.Pin_0
  3V3: U2.3V3, DHT1.Vcc, R2.Pin_0, R3.Pin_0, R1.Pin_1
  GND: U2.GND, DHT1.GND_2, S1.Pin_1, Componente1.GND
  N4: U2.D5, S1.Pin_2
  N5: U2.D6, LED2.cathode
  N6: U2.D7, LED1.cathode
  VIN: U2.Vin, Componente1.VCC
  N7: LED1.anode, R3.Pin_1
  N8: LED2.anode, R2.Pin_1
  N9: U3.GND, S2.Pin_1
  N10: U3.D5, S2.Pin_2

custom parts:
  ESP8266 NodeMCU LoLin module: ESP8266 based NodeMCU
  Humidity and Temperature Sensor DHT11: Digital relative humidity & temperature sensor DHT11
  LCD1602-I2C: A standard character display, usually with 2x16 characters. Comes in many colors with LCM1602 IIC attached.
