# Fritzing sketch sketch_v2 (saved by Fritzing 0.9.3b)
breadboards: 2

parts:
  U2 = ESP8266 NodeMCU LoLin module
  DHT1 = Humidity and Temperature Sensor DHT11
  S1 = Tilt Switch [package=THT]
  LED1 = LED - 5mm [color="Red (633nm)" package="5 mm [THT]"]
  R2 = Resistor [tolerance=±5% resistance=200 package=THT]
  R3 = Resistor [tolerance=±5% resistance=200 package=THT]
  Componente1 = LCD1602-I2C
  R1 = Resistor [tolerance=±5% resistance=10k package="0603 [SMD]"]
  U3 = ESP8266 NodeMCU LoLin module
  S2 = Tilt Switch [package=THT]
  LED2 = LED - 5mm [color="Yellow (595nm)" package="5 mm [THT]"]

nets:
  N1: U2.D3, DHT1.Data-signal, R1.Pin_0
  3V3: U2.3V3, DHT1.Vcc, R3.Pin_0, R1.Pin_1
  N2: U2.GND, DHT1.GND_2, S1.Pin_1
  N3: U2.D5, S1.Pin_2
  N4: U2.D7, LED1.cathode
  N5: LED1.anode, R3.Pin_1
  N6: R2.Pin_0, U3.3V3
  N7: R2.Pin_1, LED2.anode
  GND: Componente1.GND, U3.GND, S2.Pin_1
  VCC: Componente1.VCC, Componente1.SDA, Componente1.SCL, U3.D1, U3.D2, U3.Vin
  N8: U3.D5, S2.Pin_2
  N9: U3.D6, LED2.cathode

custom parts:
  ESP8266 NodeMCU LoLin module: ESP8266 based NodeMCU
  Humidity and Temperature Sensor DHT11: Digital relative humidity & temperature sensor DHT11
  LCD1602-I2C: A standard character display, usually with 2x16 characters. Comes in many colors with LCM1602 IIC attached.
